# Fritzing sketch Mario-Meteo_Android_Nano (saved by Fritzing 0.9.2b)
breadboards: 1

parts:
  Part1 = Arduino Nano (Rev3.0) (ICSP)
  R1 = Photocell (LDR) [package=THT]
  R2 = Resistor [tolerance=±5% resistance=220 package=THT]

nets:
  N1: Part1.D1/TX, Part1.GND, R2.Pin_0
  N2: Part1.D2, R1.pin_0, R2.Pin_1
  N3: Part1.5V, R1.pin_1

// code stored in the sketch: Mario-Meteo_Arduino_Code.ino
void setup() {
  Serial.begin(9600);
  pinMode(2, INPUT);
}

void loop() {
  Serial.print(digitalRead(2));
  delay(1000);
}
